# Fritzing sketch arduino (saved by Fritzing 0.8.5b)

parts:
  Part1 = Arduino Pro Mini v13
  DHT1 = DHT22 Humidity and Temperature Sensor
  DHT2 = DHT22 Humidity and Temperature Sensor
  NRF24L1 = NRF24L01
  Part4 = FC-28 Soil Hygrometer Module - Probe
  Part5 = FC-28 Soil Hygrometer Module
  R2 = Resistor [tolerance=±5% resistance=1M package="1206 [SMD]"]
  R3 = Resistor [tolerance=±5% resistance=3.3M package="1206 [SMD]"]
  U1 = LIPO-1000mAh [package=lipo-1000]
  Part6 = FC-28 Soil Hygrometer Module - Probe
  Part7 = FC-28 Soil Hygrometer Module
  Solar_pannel1 = solar_pannel
  CHARGER1 = USB_LiIon_LiPoly_Charger_v1.2

nets:
  N1: Part1.RAW, R2.Pin_1, U1.+, CHARGER1.batt_plus_1
  GND: Part1.GND, DHT1.GND, DHT2.GND, NRF24L1.GND, Part5.GND, R3.Pin_1, U1.-, Part7.GND, CHARGER1.batt_minus_1
  VCC: Part1.VCC, DHT1.VDD, DHT2.VDD, NRF24L1.VCC
  N2: Part1.A3, Part5.AO
  N3: Part1.A2, R2.Pin_0, R3.Pin_0
  N4: Part1.A0, Part7.AO
  N5: Part1.D13/SCK, NRF24L1.SCK
  N6: Part1.D12/MISO, NRF24L1.MISO
  N7: Part1.D11_PWM/MOSI, NRF24L1.MOSI
  VCC_2: Part1.D9_PWM, Part5.VCC, Part7.VCC
  N8: Part1.D8, NRF24L1.CSN
  N9: Part1.D7, NRF24L1.CE
  N10: Part1.D6_PWM, DHT2.DATA
  N11: Part1.D5_PWM, DHT1.DATA
  N12: Part1.D2, NRF24L1.IRQ
  N13: Part4.POS, Part5.POS
  N14: Part4.NEG, Part5.NEG
  N15: Part6.POS, Part7.POS
  N16: Part6.NEG, Part7.NEG
  N17: Solar_pannel1.aún_sin_nombre#0, CHARGER1.dcin_minus_1
  N18: Solar_pannel1.aún_sin_nombre#1, CHARGER1.dcin_plus_1

notes:
  I used a TP4056 module here
  Outside DHT22
  Inside DHT22

custom parts:
  NRF24L01: NRF24L01 module
  FC-28 Soil Hygrometer Module - Probe: The FC-28 is a soil hygrometer module that uses the Texas Instruments LM393 comparator chip to provide an analog measurement of soil humidity.
  FC-28 Soil Hygrometer Module: The FC-28 is a soil hygrometer module that uses the Texas Instruments LM393 comparator chip to provide an analog measurement of soil humidity. The digital output is high when soil moisture is over a certain threshold, as determined by adjusting the potentiometer.
  solar_pannel: Solar pannel
