# Fritzing sketch mini_eddie (saved by Fritzing 0.9.2b)

parts:
  Part1 = Arduino Pro Mini v13
  NRF24L1 = NRF24L01
  Part4 = FC-28 Soil Hygrometer Module - Probe
  Part5 = FC-28 Soil Hygrometer Module
  D1 = SOLAR-IXYS [package=solarbit-12x1]
  U1 = SWITCH_SPDT [package=kps-1290]
  U2 = Battery Holders [package=battery-aaa]
  D2 = Rectifier Diode [part_number=1N4001 package="300 mil [THT]"]
  IC1 = Switching step-up voltage regulator [package=sot23-5]

nets:
  GND: Part1.GND, NRF24L1.GND, Part5.GND, D1.C, U2.-, IC1.OUT
  N1: Part1.VCC, IC1.EN
  N2: Part1.A3, U1.P, U2.+
  N3: Part1.A2, Part5.AO
  N4: Part1.D13/SCK, NRF24L1.SCK
  N5: Part1.D12/MISO, NRF24L1.MISO
  N6: Part1.D11_PWM/MOSI, NRF24L1.MOSI
  N7: Part1.D9_PWM, NRF24L1.VCC
  N8: Part1.D8, NRF24L1.CSN
  N9: Part1.D7, NRF24L1.CE
  N10: Part1.D4, Part5.VCC
  N11: Part1.D2, NRF24L1.IRQ
  N12: Part4.POS, Part5.NEG
  N13: Part4.NEG, Part5.POS
  N14: D1.A, D2.anode
  N15: U1.O, D2.cathode, IC1.NC

notes:
  DC/DC Boost converter 0.8-3v -> 3.3v

custom parts:
  NRF24L01: NRF24L01 module
  FC-28 Soil Hygrometer Module - Probe: The FC-28 is a soil hygrometer module that uses the Texas Instruments LM393 comparator chip to provide an analog measurement of soil humidity.
  FC-28 Soil Hygrometer Module: The FC-28 is a soil hygrometer module that uses the Texas Instruments LM393 comparator chip to provide an analog measurement of soil humidity. The digital output is high when soil moisture is over a certain threshold, as determined by adjusting the potentiometer.
