# Fritzing sketch raspberrypi (saved by Fritzing 0.8.5b)

parts:
  Raspberry_Pi_B_rev1 = Raspberry Pi B rev2
  NRF24L1 = NRF24L01

nets:
  N1: Raspberry_Pi_B_rev1.GPIO_22, NRF24L1.CE
  N2: Raspberry_Pi_B_rev1.GPIO_10, NRF24L1.MOSI
  N3: Raspberry_Pi_B_rev1.GPIO_9, NRF24L1.MISO
  N4: Raspberry_Pi_B_rev1.GPIO_11, NRF24L1.SCK
  N5: Raspberry_Pi_B_rev1.GPIO_8, NRF24L1.CSN
  GND: Raspberry_Pi_B_rev1.GND, NRF24L1.GND
  3V3: Raspberry_Pi_B_rev1.3V3, NRF24L1.VCC

custom parts:
  NRF24L01: NRF24L01 module
